# Fritzing sketch Sensor (saved by Fritzing 0.9.3b)
breadboards: 1

parts:
  Part1 = Arduino Pro Mini (3.3V)
  RHT1 = Humidity and Temperature Sensor RHT03
  Part3 = NRF24L01
  R1 = Resistor [tolerance=±5% resistance=1k package="2010 [SMD]"]
  Part2 = Breadboard Power Supply Board SMD

nets:
  GND: Part1.GND, RHT1.GND_2, Part3.GND, Part2.GND
  VCC: Part1.VCC, RHT1.Vcc, Part3.VCC, R1.Pin_1, Part2.VCC
  N1: Part1.SCK, Part3.SCK
  N2: Part1.MISO, Part3.MISO
  N3: Part1.MOSI, Part3.MOSI
  N4: Part1.D10, Part3.CSN
  N5: Part1.D9, Part3.CE
  N6: Part1.D2, RHT1.Data-signal, RHT1.GND_1, R1.Pin_0
